# Fritzing sketch Brazo (saved by Fritzing 0.9.3b)
breadboards: 2

parts:
  Componente1 = Arduino Uno (Rev3) - ICSP
  U1 = POT [package=pot_mammoth]
  LCD1 = LCD screen
  S5 = Pushbutton [package=THT]
  R5 = Resistor [tolerance=±5% resistance=1k package="2512 [SMD]"]
  R6 = Resistor [tolerance=±5% resistance=220 package="2512 [SMD]"]
  LED1 = Super Flux LED blue [color=Blue]
  R7 = Resistor [tolerance=±5% resistance=1k package="2512 [SMD]"]

nets:
  N1: Componente1.ICSP_MISO, Componente1.D12/MISO, LCD1.RS
  N2: Componente1.ICSP_MOSI, Componente1.D11_PWM/MOSI, LCD1.R/W
  N3: Componente1.D2, S5.leg1
  N4: Componente1.D3_PWM, LED1.cathode
  N5: Componente1.D4, LCD1.DB6
  N6: Componente1.D5_PWM, LCD1.DB5
  N7: Componente1.D6_PWM, LCD1.DB4
  N8: Componente1.D7, LCD1.DB3
  5V: Componente1.5V, U1.S, LCD1.VDD, R5.Pin_0, R6.Pin_0
  GND: Componente1.GND, U1.E, LCD1.VSS, LCD1.LED-, R7.Pin_0
  N9: U1.A, LCD1.V0
  N10: LCD1.LED+, R6.Pin_1
  N11: S5.leg0, R5.Pin_1
  N12: LED1.anode, R7.Pin_1
