# Fritzing sketch Brazo_I2C (saved by Fritzing 0.9.3b)
breadboards: 2

parts:
  Componente1 = Arduino Uno (Rev3) - ICSP
  U1 = POT [package=pot_mammoth]
  LCD1 = LCD screen
  S5 = Pushbutton [package=THT]
  R5 = Resistor [tolerance=±5% resistance=220 package="2512 [SMD]"]
  R6 = Resistor [tolerance=±5% resistance=220 package="2512 [SMD]"]
  LED1 = Super Flux LED blue [color=Red]
  R7 = Resistor [tolerance=±5% resistance=1k package="2512 [SMD]"]
  Componente2 = MicroSD Card Module
  Componente3 = Arduino Uno (Rev3) - ICSP
  LED2 = Super Flux LED blue [color=Blue]
  R8 = Resistor [tolerance=±5% resistance=220 package="2512 [SMD]"]
  J1 = Basic Servo
  J3 = Basic Servo
  J4 = Basic Servo

nets:
  N1: Componente1.A0, LED1.cathode
  N2: Componente1.A1, LED2.cathode
  GND: Componente1.A2, Componente1.GND, U1.E, LCD1.VSS, LCD1.R/W, LCD1.LED-, S5.leg1, R5.Pin_0, Componente2.GND, Componente3.GND, R8.Pin_0, J1.gnd, J3.gnd, J4.gnd
  N3: Componente1.A4/SDA, Componente3.A4/SDA
  N4: Componente1.A5/SCL, Componente3.A5/SCL
  N5: Componente1.ICSP_MOSI, Componente1.D11_PWM/MOSI, J1.pulse
  N6: Componente1.D12/MISO, J3.pulse
  N7: Componente1.D13/SCK, J4.pulse
  N8: Componente1.D1/TX, LCD1.RS
  N9: Componente1.D2, LCD1.E
  N10: Componente1.D3_PWM, LCD1.DB3
  N11: Componente1.D4, LCD1.DB4
  N12: Componente1.D5_PWM, LCD1.DB5
  N13: Componente1.D6_PWM, LCD1.DB6
  VCC: Componente1.5V, J1.vcc, J3.vcc, J4.vcc
  VDD: U1.S, LCD1.VDD, R6.Pin_0, R7.Pin_0, Componente2.VCC, Componente3.5V
  N14: U1.A, LCD1.V0
  N15: LCD1.LED+, R6.Pin_1
  N16: S5.leg0, R7.Pin_1
  N17: R5.Pin_1, LED1.anode
  N18: Componente2.MISO, Componente3.ICSP_MISO, Componente3.D12/MISO
  N19: Componente2.MOSI, Componente3.ICSP_MOSI, Componente3.D11_PWM/MOSI
  N20: Componente2.SCK, Componente3.D13/SCK
  N21: Componente2.CS, Componente3.D9_PWM
  N22: LED2.anode, R8.Pin_1
