# Fritzing sketch Java-Arduino-LCD (saved by Fritzing 0.9.3b)
breadboards: 2

parts:
  Componente1 = Arduino Uno (Rev3) - ICSP
  U1 = POT [package=pot_mammoth]
  LCD1 = LCD screen
  T1 = LM35 Temperature Sensor [package="TO92 [THT]"]
  S1 = Pushbutton [package=THT]
  S2 = Pushbutton [package=THT]
  S3 = Pushbutton [package=THT]
  S4 = Pushbutton [package=THT]
  S5 = Pushbutton [package=THT]
  R1 = Resistor [tolerance=±5% resistance=1k package="2512 [SMD]"]
  R2 = Resistor [tolerance=±5% resistance=1k package="2512 [SMD]"]
  R3 = Resistor [tolerance=±5% resistance=1k package="2512 [SMD]"]
  R4 = Resistor [tolerance=±5% resistance=1k package="2512 [SMD]"]
  R5 = Resistor [tolerance=±5% resistance=1k package="2512 [SMD]"]
  R6 = Resistor [tolerance=±5% resistance=220 package="2512 [SMD]"]
  U2 = POT [package=pot_mammoth]
  Componente2 = Real Time Clock Module - DS1307 RTC Breakout Board

nets:
  N1: Componente1.A0, U2.A
  N2: Componente1.A2, T1.Vout
  N3: Componente1.A4/SDA, Componente2.SQW
  N4: Componente1.A5/SCL, Componente2.GND
  N5: Componente1.ICSP_MOSI, Componente1.D11_PWM/MOSI, LCD1.R/W
  N6: Componente1.D8, S3.leg0, R3.Pin_0
  N7: Componente1.D9_PWM, S4.leg0, R4.Pin_0
  N8: Componente1.D10_PWM/SS, S5.leg0, R5.Pin_0
  N9: Componente1.D12/MISO, LCD1.RS
  N10: Componente1.D2, LCD1.DB6
  N11: Componente1.D3_PWM, LCD1.DB5
  N12: Componente1.D4, LCD1.DB4
  N13: Componente1.D5_PWM, LCD1.DB3
  N14: Componente1.D6_PWM, S1.leg0, R1.Pin_0
  N15: Componente1.D7, S2.leg0, R2.Pin_0
  N16: U1.S, LCD1.VDD, T1.+Vs, R1.Pin_1, R2.Pin_1, R3.Pin_1, R4.Pin_1, R5.Pin_1, R6.Pin_0, U2.S, Componente2.SCL
  N17: U1.A, LCD1.V0
  VSS: U1.E, LCD1.VSS, LCD1.LED-, T1.GND, S1.leg1, S2.leg1, S3.leg1, S4.leg1, S5.leg1, U2.E, Componente2.SDA
  N18: LCD1.LED+, R6.Pin_1
