# Fritzing sketch Puerta (saved by Fritzing 0.9.3b)
breadboards: 1

parts:
  Componente1 = Arduino Uno (Rev3) - ICSP
  LED1 = Super Flux RGB LED (com. cathode)
  S1 = Reed switch [package=THT]
  R1 = Resistor [tolerance=±5% resistance=220 package=THT]
  R2 = Resistor [tolerance=±5% resistance=220 package=THT]
  R3 = Resistor [tolerance=±5% resistance=220 package=THT]
  R4 = Resistor [tolerance=±5% resistance=330 package=THT]
  R5 = Resistor [tolerance=±5% resistance=1k package=THT]
  LED2 = RGB LED (com. cathode, rbg) [color="Red (633nm)" package="5 mm [THT]"]

nets:
  N1: Componente1.D9_PWM, R2.Pin_0
  N2: Componente1.D10_PWM/SS, R3.Pin_0
  N3: Componente1.D11_PWM/MOSI, R1.Pin_0
  N4: Componente1.D13/SCK, LED1.red_anode, LED1.common_cathode
  N5: Componente1.D2, Componente1.5V, R5.Pin_0, LED2.common_cathode
  N6: Componente1.GND, S1.pin_2, R4.Pin_0
  N7: LED1.blue_anode, LED1.green_anode, R4.Pin_1
  N8: S1.pin_1, R5.Pin_1
  N9: R1.Pin_1, LED2.green_anode
  N10: R2.Pin_1, LED2.red_anode
  N11: R3.Pin_1, LED2.blue_anode
